# Fritzing sketch circuit (saved by Fritzing 0.9.3b)
perfboards: 1

parts:
  R2 = Resistor [tolerance=±5% resistance=1k package=THT]
  C1 = Electrolytic Capacitor [capacitance=1000µF package="300 mil [THT, electrolytic]"]
  Composant1 = Arduino Pro Mini v13
  Raspberry_Pi_B_rev1 = Raspberry Pi B rev1
  Composant2 = Adafruit DS3231 [part_number="Adafruit #3013"]
  U4 = RELAY-2 [package=relay-g5v]
  Q1 = NPN-Transistor [package="TO92 [THT]"]
  Couvercle = Toggle Switch [package=THT]

nets:
  N1: R2.Pin_0, Composant1.D9_PWM
  N2: R2.Pin_1, Q1.B
  N3: C1.-, Q1.E
  5V: C1.+, Composant1.RAW, U4.6, U4.9
  VCC: Composant1.VCC, Composant2.Vin
  GND: Composant1.GND, Raspberry_Pi_B_rev1.GND, Composant2.GND, Couvercle.L1
  N4: Composant1.A4, Composant2.SDA
  N5: Composant1.A5, Composant2.SCL
  N6: Composant1.D3_PWM, Composant2.SQW
  N7: Composant1.D2, Couvercle.COM
  N8: Raspberry_Pi_B_rev1.5V, U4.2
  N9: U4.1, Q1.C

custom parts:
  Adafruit DS3231: The datasheet for the DS3231 explains that this part is an "Extremely Accurate I²C-Integrated RTC/TCXO/Crystal". And, hey, it does exactly what it says on the tin! This Real Time Clock (RTC) is the most precise you can get in a small, low power package. Most RTCs use an external 32kHz timing crystal that is used to keep time with low current draw. And that's all well and good, but those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
